# Fritzing sketch sonda (saved by Fritzing 0.9.3b)

parts:
  Componente2 = Arduino Ethernet Shield (Rev3)
  Componente3 = Arduino Mega 2560 (Rev3)
  DS1 = DS18B20 1-Wire Temperature Sensor [part_number=DS18B20]
  R1 = Resistor [tolerance=±5% resistance=4.7k package="0402 [SMD]"]
  Conductivity_Circuit1 = Conductivity Circuit
  Pre-Assembled_Female_BNC1 = Pre-Assembled Female BNC
  MPX4250AP1 = MPX4250AP pressure sensor [part_number=MPX]

nets:
  N1: Componente2.A1, Conductivity_Circuit1.PRB
  N2: Componente2.A2, MPX4250AP1.V_out
  N3: Componente2.D2, DS1.DQ, R1.Pin_0
  5V: Componente2.5V, Conductivity_Circuit1.Vcc
  GND: Componente2.GND, Conductivity_Circuit1.GND
  5V_2: Componente3.5V, DS1.VDD, R1.Pin_1, MPX4250AP1.Vs
  GND_2: Componente3.GND, DS1.GND, MPX4250AP1.GND
  N4: Conductivity_Circuit1.TX, Pre-Assembled_Female_BNC1.PRB
  N5: Conductivity_Circuit1.RX, Pre-Assembled_Female_BNC1.NC
